# Fritzing sketch HC-SR04 (saved by Fritzing 0.9.9b)

parts:
  Raspberry_Pi_1 = Raspberry Pi 3 [part_number=RPI-3-V1.2]
  HC-SR04_Sensor_1 = HC-SR04 Ultrasonic Distance Sensor

nets:
  N1: Raspberry_Pi_1.GIPO17, HC-SR04_Sensor_1.TRIG
  N2: Raspberry_Pi_1.GIPO18, HC-SR04_Sensor_1.ECHO
  GND: Raspberry_Pi_1.GND, HC-SR04_Sensor_1.GND
  5V: Raspberry_Pi_1.5V, HC-SR04_Sensor_1.VCC
